# Fritzing sketch Halloweenio (saved by Fritzing 0.9.3b)
circuit board: 6.88566cm x 5.36311cm
breadboards: 1

parts:
  Part1 = Arduino Uno (Rev3)
  S1 = Pushbutton [package="[THT]"]
  R1 = Resistor [tolerance=±5% resistance=1k package=THT]
  T1 = NPN-Transistor [package="TO92 [THT]"]
  Q2 = NPN-Transistor [package="TO92 [THT]"]
  Q3 = NPN-Transistor [package="TO92 [THT]"]
  R2 = Resistor [tolerance=±5% resistance=1k package=THT]
  R3 = Resistor [tolerance=±5% resistance=1k package=THT]
  R4 = Resistor [tolerance=±5% resistance=1k package=THT]
  R5 = Resistor [tolerance=±5% resistance=1k package=THT]
  Q4 = NPN-Transistor [package="TO92 [THT]"]
  Q5 = NPN-Transistor [package="TO92 [THT]"]
  PIR1 = PIR sensor
  R6 = Resistor [tolerance=±5% resistance=1k package=THT]

nets:
  N1: Part1.D8, R2.Pin_0
  N2: Part1.D9_PWM, R3.Pin_0
  N3: Part1.D10_PWM/SS, R4.Pin_0
  N4: Part1.D11_PWM/MOSI, R5.Pin_0
  N5: Part1.D12/MISO, R6.Pin_0
  N6: Part1.D2, S1.Pin_1, S1.Pin_2, R1.Pin_0
  N7: Part1.D3_PWM, PIR1.SIG
  5V: Part1.5V, S1.Pin_3, S1.Pin_4, PIR1.VDD
  GND: Part1.GND, R1.Pin_1, T1.E, Q2.E, Q3.E, Q4.E, Q5.E, PIR1.GND
  N8: T1.B, R2.Pin_1
  N9: Q2.B, R3.Pin_1
  N10: Q3.B, R4.Pin_1
  N11: R5.Pin_1, Q4.B
  N12: Q5.B, R6.Pin_1
